# Fritzing sketch hcs05 (saved by Fritzing 0.9.3b)
breadboards: 1

parts:
  R1 = Resistor [tolerance=±5% resistance=220 package=THT]
  hc-sr1 = hc-sr04
  Launchpad1 = TI Launchpad MSP430G2

nets:
  N1: R1.Pin_0, hc-sr1.GND
  N2: hc-sr1.Trig, Launchpad1.p13
  N3: hc-sr1.Echo, Launchpad1.p14
