# Fritzing sketch motor (saved by Fritzing 0.9.3b)
breadboards: 1

parts:
  Launchpad1 = TI Launchpad MSP430G2
  IC1 = L293D [package=THT]
  M1 = DC Motor
  M2 = DC Motor
  LED1 = smd LED [color="Red (633nm)" package="1206 [SMD]"]
  LED2 = smd LED [color="Red (633nm)" package="1206 [SMD]"]
  LED3 = smd LED [color="Red (633nm)" package="1206 [SMD]"]
  LED4 = smd LED [color="Red (633nm)" package="1206 [SMD]"]
  VCC1 = Battery block 9V
  Grove2 = Grove Infrared Receiver
  Grove1 = Grove Infrared Receiver
  R1 = Resistor [tolerance=±5% resistance=220 package=THT]
  R2 = Resistor [tolerance=±5% resistance=220 package=THT]
  hc-sr1 = hc-sr04
  R3 = Resistor [tolerance=±5% resistance=220 package=THT]
  Grove3 = Grove Infrared Receiver
  Grove4 = Grove Infrared Receiver
  R4 = Resistor [tolerance=±5% resistance=220 package=THT]
  R5 = Resistor [tolerance=±5% resistance=220 package=THT]

nets:
  N1: Launchpad1.p10, hc-sr1.Trig
  N2: Launchpad1.p9, hc-sr1.Echo
  VCC: Launchpad1.p1, Grove2.VCC, Grove1.VCC, hc-sr1.VCC, Grove3.VCC, Grove4.VCC
  N3: Launchpad1.p12, Grove4.GND, R5.Pin_1
  N4: Launchpad1.p13, Grove1.GND, R2.Pin_1
  N5: Launchpad1.p14, IC1.Enable_1
  N6: Launchpad1.p20, IC1.0V, R1.Pin_0, R2.Pin_0, R3.Pin_0, R4.Pin_0, R5.Pin_0
  N7: IC1.Out_1_(_Controlled_by_Enable_1_), M1.pin_2, M2.pin_1, LED1.anode, LED2.cathode
  N8: IC1.+Vmotor, LED2.anode, LED4.anode
  N9: IC1.+V, VCC1.+
  N10: M1.pin_1, M2.pin_2, LED3.anode, LED4.cathode
  N11: LED1.cathode, LED3.cathode, VCC1.-
  N12: Grove2.GND, R1.Pin_1
  N13: hc-sr1.GND, R3.Pin_1
  N14: Grove3.GND, R4.Pin_1
