# Fritzing sketch placa (saved by Fritzing 0.9.3b)
breadboards: 1

parts:
  IC1 = PICAXE-20M [package=THT]
  IC2 = L293D [package=THT]
  VCC1 = Battery block 9V
  U1 = Voltage Regulator - 3.3V [package="TO220 [THT]"]
  U2 = Voltage Regulator - 5V [package="TO220 [THT]"]
  M1 = DC Motor
  M2 = DC Motor
  hc-sr1 = hc-sr04
  Grove1 = Grove Infrared Receiver
  Grove2 = Grove Infrared Emitter
  R1 = Resistor [tolerance=±5% resistance=680 package="2512 [SMD]"]
  R2 = Resistor [tolerance=±5% resistance=680 package="2512 [SMD]"]
  R3 = Resistor [tolerance=±5% resistance=680 package="2512 [SMD]"]
  R4 = Resistor [tolerance=±5% resistance=680 package="2512 [SMD]"]
  Grove4 = Grove Infrared Emitter
  Grove3 = Grove Infrared Receiver

nets:
  N1: IC1.+V, U1.output_voltage
  N2: IC1.Serial_In, IC2.Enable_1
  N3: IC1.In_5, IC2.In_1
  N4: IC1.In_4, IC2.In_2
  N5: IC1.In_1_/_ADC_1, Grove2.TX
  N6: IC1.In_0_/_Infrain, Grove1.RX
  N7: IC1.Out_6, Grove4.TX
  N8: IC1.Out_5, hc-sr1.Echo
  N9: IC1.Out_4, hc-sr1.Trig
  N10: IC1.Out_2, IC2.In_3
  N11: IC1.Out_1, IC2.In_4
  N12: IC1.Out_0_/_Infraout, IC2.Enable_2
  N13: IC2.Out_1_(_Controlled_by_Enable_1_), M2.pin_2
  GND: IC2.0V, VCC1.-, U1.GND, U2.GND, hc-sr1.GND, Grove1.GND, Grove2.GND, Grove4.GND, Grove3.GND
  N14: IC2.Out_2_(_Controlled_by_Enable_1_), M2.pin_1
  N15: IC2.+Vmotor, VCC1.+, U1.input_voltage, U2.input_voltage, R1.Pin_0, R2.Pin_0, R3.Pin_0, R4.Pin_0
  N16: IC2.Out_3_(_Controlled_by_Enable_2_), M1.pin_1
  N17: IC2.Out_4_(_Controlled_by_Enable_2_), M1.pin_2
  N18: IC2.+V, U2.output_voltage, hc-sr1.VCC
  N19: Grove1.VCC, R4.Pin_1
  N20: Grove2.VCC, R1.Pin_1
  N21: R2.Pin_1, Grove4.VCC
  N22: R3.Pin_1, Grove3.VCC
