# Fritzing sketch ultimo (saved by Fritzing 0.9.3b)
breadboards: 1

parts:
  Launchpad1 = TI Launchpad MSP430G2
  IC1 = L293D [package=THT]
  M1 = DC Motor
  M2 = DC Motor
  VCC1 = Battery block 9V
  hc-sr1 = hc-sr04
  Grove1 = Grove Infrared Receiver
  Grove2 = Grove Infrared Emitter
  R1 = Resistor [tolerance=±5% resistance=220 package="0603 [SMD]"]
  R2 = Resistor [tolerance=±5% resistance=220 package="0603 [SMD]"]

nets:
  N1: Launchpad1.p8, hc-sr1.Echo
  N2: Launchpad1.p7, IC1.In_3
  N3: Launchpad1.p6, IC1.In_4
  N4: Launchpad1.p5, IC1.Enable_2
  N5: Launchpad1.p4, hc-sr1.Trig
  N6: Launchpad1.p1, IC1.+V, hc-sr1.VCC, R1.Pin_1, R2.Pin_1
  N7: Launchpad1.p11, IC1.In_2
  N8: Launchpad1.p12, IC1.In_1
  N9: Launchpad1.p13, IC1.Enable_1, Grove1.RX
  N10: Launchpad1.p14, Grove2.TX
  N11: Launchpad1.p20, IC1.0V, VCC1.-, hc-sr1.GND
  N12: IC1.Out_1_(_Controlled_by_Enable_1_), M2.pin_2
  N13: IC1.Out_2_(_Controlled_by_Enable_1_), M2.pin_1
  N14: IC1.+Vmotor, VCC1.+
  N15: IC1.Out_3_(_Controlled_by_Enable_2_), M1.pin_2
  N16: IC1.Out_4_(_Controlled_by_Enable_2_), M1.pin_1
  GND: Grove1.GND, Grove2.GND
  N17: Grove1.VCC, R2.Pin_0
  N18: Grove2.VCC, R1.Pin_0
